// Digital circuit Corrimiento.dig as structural Verilog
module Corrimiento (
  input  A3,
  input  A2,
  input  A1,
  input  A0,
  input  in_9,
  input  clk,
  input  A4,
  input  A3_2,
  input  A2_2,
  input  A1_2,
  input  A0_2,
  input  in_16,
  input  in_17,
  input  in_18,
  input  clk_2,
  input  in_23,
  input  clk_3,
  input  clk_4,
  input  in_32,
  input  in_33,
  input  in_34,
  input  in_36,
  input  clk_5,
  input  in_41,
  input  in_42,
  input  in_43,
  input  clk_6,
  input  in_49,
  input  in_50,
  input  in_51,
  input  in_53,
  input  clk_7,
  input  in_58,
  input  in_59,
  input  in_60,
  input  in_62,
  input  in_63,
  output out_5,
  output out_6,
  output out_7,
  output out_8,
  output out_19,
  output out_20,
  output out_21,
  output out_25,
  output out_26,
  output out_27,
  output out_29,
  output out_30,
  output out_31,
  output out_35,
  output out_38,
  output out_39,
  output out_40,
  output out_44,
  output out_46,
  output out_47,
  output out_48,
  output out_52,
  output out_55,
  output out_56,
  output out_57,
  output out_61
);

  wire add_1_s, add_2_c_o, add_2_s, add_3_c_o, add_3_s, add_4_c_o, add_4_s, and_1_out, and_2_out, and_3_out,
       and_4_out, d_ff_12_q, d_ff_13_q, d_ff_14_q, d_ff_15_q, d_ff_16_q, d_ff_17_q, d_ff_18_q, d_ff_19_q,
       d_ff_20_q, d_ff_21_q, d_ff_22_q, d_ff_23_q, d_ff_24_q, d_ff_25_q, d_ff_26_q, d_ff_27_q, or_14_out,
       xor_1_out, xor_2_out, xor_3_out, xor_4_out;

  xor xor_1 (xor_1_out, A3, in_9);
  xor xor_2 (xor_2_out, A2, in_9);
  xor xor_3 (xor_3_out, A1, in_9);
  xor xor_4 (xor_4_out, A0, in_9);
  Add add_1 (.a(out_8), .b(xor_1_out), .c_i(add_2_c_o), .s(add_1_s));  // open: c_o
  Add add_2 (.a(out_7), .b(xor_2_out), .c_i(add_3_c_o), .s(add_2_s), .c_o(add_2_c_o));
  Add add_3 (.a(out_6), .b(xor_3_out), .c_i(add_4_c_o), .s(add_3_s), .c_o(add_3_c_o));
  Add add_4 (.a(out_5), .b(xor_4_out), .c_i(in_9), .s(add_4_s), .c_o(add_4_c_o));
  D_FF d_ff_1 (.D(in_16), .C(clk_2), .Q(out_19));  // open: nQ
  D_FF d_ff_2 (.D(in_17), .C(clk_2), .Q(out_20));  // open: nQ
  D_FF d_ff_3 (.D(in_18), .C(clk_2), .Q(out_21));  // open: nQ
  D_FF d_ff_4 (.D(add_1_s), .C(clk), .Q(out_8));  // open: nQ
  D_FF d_ff_5 (.D(add_2_s), .C(clk), .Q(out_7));  // open: nQ
  D_FF d_ff_6 (.D(add_3_s), .C(clk), .Q(out_6));  // open: nQ
  D_FF d_ff_7 (.D(add_4_s), .C(clk), .Q(out_5));  // open: nQ
  D_FF d_ff_8 (.D(in_23), .C(clk_3), .Q(out_27));  // open: nQ
  D_FF d_ff_9 (.D(out_27), .C(clk_3), .Q(out_26));  // open: nQ
  D_FF d_ff_10 (.D(out_26), .C(clk_3), .Q(out_25));  // open: nQ
  D_FF d_ff_11 (.D(in_36), .C(clk_4), .Q(out_35));  // open: nQ
  D_FF d_ff_12 (.D(out_35), .C(clk_4), .Q(d_ff_12_q));  // open: nQ
  D_FF d_ff_13 (.D(out_31), .C(clk_4), .Q(d_ff_13_q));  // open: nQ
  D_FF d_ff_14 (.D(out_30), .C(clk_4), .Q(d_ff_14_q));  // open: nQ
  or or_1 (out_31, in_32, d_ff_12_q);
  or or_2 (out_30, in_33, d_ff_13_q);
  or or_3 (out_29, in_34, d_ff_14_q);
  D_FF d_ff_15 (.D(in_53), .C(clk_6), .Q(d_ff_15_q));  // open: nQ
  D_FF d_ff_16 (.D(out_52), .C(clk_6), .Q(d_ff_16_q));  // open: nQ
  D_FF d_ff_17 (.D(out_48), .C(clk_6), .Q(d_ff_17_q));  // open: nQ
  D_FF d_ff_18 (.D(out_47), .C(clk_6), .Q(d_ff_18_q));  // open: nQ
  D_FF d_ff_19 (.D(1'b0), .C(clk_5), .Q(d_ff_19_q));  // open: nQ
  D_FF d_ff_20 (.D(out_44), .C(clk_5), .Q(d_ff_20_q));  // open: nQ
  D_FF d_ff_21 (.D(out_40), .C(clk_5), .Q(d_ff_21_q));  // open: nQ
  D_FF d_ff_22 (.D(out_39), .C(clk_5), .Q(d_ff_22_q));  // open: nQ
  RS_FF_AS rs_ff_as_1 (.S(d_ff_16_q), .R(d_ff_15_q), .nQ(out_52));  // open: Q
  or or_4 (out_48, in_49, d_ff_16_q);
  or or_5 (out_47, in_50, d_ff_17_q);
  or or_6 (out_46, in_51, d_ff_18_q);
  RS_FF_AS rs_ff_as_2 (.S(d_ff_20_q), .R(d_ff_19_q), .nQ(out_44));  // open: Q
  or or_7 (out_40, in_41, d_ff_20_q);
  or or_8 (out_39, in_42, d_ff_21_q);
  or or_9 (out_38, in_43, d_ff_22_q);
  D_FF d_ff_23 (.D(1'b0), .C(clk_7), .Q(d_ff_23_q));  // open: nQ
  D_FF d_ff_24 (.D(out_61), .C(clk_7), .Q(d_ff_24_q));  // open: nQ
  D_FF d_ff_25 (.D(out_57), .C(clk_7), .Q(d_ff_25_q));  // open: nQ
  D_FF d_ff_26 (.D(out_56), .C(clk_7), .Q(d_ff_26_q));  // open: nQ
  or or_10 (out_61, and_1_out, d_ff_23_q);
  or or_11 (out_57, and_2_out, d_ff_24_q);
  or or_12 (out_56, and_3_out, d_ff_25_q);
  or or_13 (out_55, and_4_out, d_ff_26_q);
  and and_1 (and_1_out, d_ff_27_q, in_62);
  and and_2 (and_2_out, d_ff_27_q, in_58);
  and and_3 (and_3_out, d_ff_27_q, in_59);
  and and_4 (and_4_out, d_ff_27_q, in_60);
  or or_14 (or_14_out, in_63, 1'b0);
  D_FF #(.Default(1)) d_ff_27 (.D(or_14_out), .C(clk_7), .Q(d_ff_27_q));  // open: nQ

  assign A1_2 = A0_2;
  assign A2_2 = A0_2;
  assign A3_2 = A0_2;
  assign A4 = A0_2;
endmodule
